# Fritzing sketch circuit diagram (saved by Fritzing 0.9.1b)
breadboards: 2

parts:
  Part1 = Arduino Uno (Rev3)
  M1 = DC Motor
  M2 = DC Motor
  IC1 = H-Bridge [package=THT]
  BATT1 = 4xAA Switchable Battery Pack w/Bare Wire
  BAT1 = BC9VPC [package=bc9vpc]

nets:
  N1: Part1.D8, IC1.1_2EN
  N2: Part1.D9_PWM, IC1.4A
  N3: Part1.D10_PWM/SS, IC1.3_4EN
  N4: Part1.D3_PWM, IC1.1A
  N5: Part1.D5_PWM, IC1.2A
  N6: Part1.D6_PWM, IC1.3A
  N7: Part1.5V, IC1.VCC1
  GND: Part1.GND, IC1.GND1, IC1.GND2, IC1.GND3, IC1.GND4, BATT1.NEG, BAT1.V-
  N8: Part1.VIN, BAT1.V+
  N9: M1.pin_1, IC1.4Y
  N10: M1.pin_2, IC1.3Y
  N11: M2.pin_1, IC1.2Y
  N12: M2.pin_2, IC1.1Y
  N13: IC1.VCC2, BATT1.POS

notes:
  ULTRASONIC SENSOR
  blue (pin 12) = trigger
  green (pin 11) = echo
  5V and GND

custom parts:
  4xAA Switchable Battery Pack w/Bare Wire: 4xAA Switchable Battery Pack with Bare Wire connection
